// Logisim project project.circ as structural Verilog: 7 circuits, main circuit main
module main (
  output [1:0] out_1
);

  wire A, AE, aluIMM, aluSelect, and_2_out, and_3_out, and_4_out, and_5_out, and_6_out, and_7_out, B, BE,
       bit_extender_2_out, CF, clear, clock, cmp, E, ISJ, J, memoryL, memoryS, not_1_out, not_2_out, we, ZF;
  wire [1:0] CMP_zf;
  wire [3:0] dreg, op, sreg, treg;
  wire [7:0] adrs;
  wire [11:0] loc;
  wire [15:0] adder_1_out, adder_2_out, bit_extender_1_out, multiplexer_1_out, PC_q, rom_1_data, source1,
       source2;

  Clock clock_1 (.out(clock));
  Button button_1 (.out(clear));
  Adder #(.width(16)) adder_1 (.a(PC_q), .b(16'h1), .out(adder_1_out));  // open: cin, cout
  Adder #(.width(16)) adder_2 (.a(adder_1_out), .b(bit_extender_1_out), .out(adder_2_out));  // open: cin, cout
  assign bit_extender_1_out = {{4{loc[11]}}, loc};  // Bit_Extender bit_extender_1
  Bit_Extender #(.in_width(12), .out_width(1)) bit_extender_2 (.in(loc), .out(bit_extender_2_out));
  and and_1 (out_1[1], bit_extender_2_out, out_1[0]);
  Multiplexer #(.select(2), .width(16), .enable("false")) multiplexer_1 (
    .in0(adder_1_out), .in2(bit_extender_1_out), .in3(adder_2_out), .out(multiplexer_1_out), .sel(out_1));  // open: in1
  Register #(.width(16)) PC (.D(multiplexer_1_out), .en(1'b1), .Q(PC_q), .clk(clock), .clr(clear));
  compare u_CMP (.src1(source1), .src2(source2), .CF(CMP_zf[1]), .ZF(CMP_zf[0]));
  control_unit CU (
    .opcode(op), .Compare(cmp), .aluSlc(aluSelect), .aluImm(aluIMM), .regWE(we), .memLoad(memoryL),
    .memSt(memoryS), .jumpA(A), .jmpRn(J), .jump(ISJ), .jumpAE(AE), .jumpB(B), .jumpE(E), .jumpBE(BE));  // open: regSelect
  Register #(.width(2)) register_1 (.D(CMP_zf), .en(cmp), .Q({CF, ZF}), .clk(clock), .clr(clear));
  ROM #(.addrWidth(16), .dataWidth(16)) rom_1 (.addr(PC_q), .data(rom_1_data), .sel(1'b1));
  IR IR (
    .in_1(rom_1_data), .clock(clock), .clear(clear), .opcode(op), .location(loc), .address(adrs),
    .treg(treg), .sreg(sreg), .dreg(dreg));
  not not_1 (not_1_out, ZF);
  not not_2 (not_2_out, CF);
  and and_2 (and_2_out, not_1_out, CF, B);
  and and_3 (and_3_out, ZF, CF, BE);
  and and_4 (and_4_out, ZF, not_2_out, E);
  and and_5 (and_5_out, not_1_out, not_2_out, A);
  and and_6 (and_6_out, not_2_out, AE);
  and and_7 (and_7_out, J, J, J);
  or or_1 (out_1[0], and_2_out, and_3_out, and_4_out, and_5_out, and_6_out, and_7_out);
  datapath DP (
    .address(adrs), .read_reg1(treg), .read_reg2(sreg), .aluImmVal(treg), .write_reg(dreg), .we(we),
    .regClc(clock), .reset(clear), .memStore(memoryS), .memLoad(memoryL), .aluImm(aluIMM),
    .aluSlc(aluSelect), .src1(source1), .src2(source2));  // open: dmOUT

  // Other names for the same wires on the sheet: JC = out_1[0]; ss[1:0] = out_1

  // Notes on the sheet:
  //   contents of rom_1 (hex, n*v repeats v):
  //   4201 4302 123 1424 3003 6012 a000 6012 b000 6014 c000 6021 9000 6031 7ff9
endmodule

module control_unit (
  input  [3:0] opcode,
  output Compare,
  output aluSlc,
  output regSelect,
  output aluImm,
  output regWE,
  output memLoad,
  output memSt,
  output jumpA,
  output jmpRn,
  output jump,
  output jumpAE,
  output jumpB,
  output jumpE,
  output jumpBE
);

  wire add, addi, \and , andi, decoder_1_out12, decoder_1_out13, decoder_1_out14, decoder_1_out15, ja, jae,
       jb, jbe, je, jmp, ld, st;

  or or_1 (aluSlc, \and , andi);
  or or_2 (aluImm, addi, andi);
  Decoder #(.select(4), .enable("false")) decoder_1 (
    .out0(add), .out1(addi), .out2(\and ), .out3(andi), .out4(ld), .out5(st), .out6(Compare), .out7(jmp),
    .out8(jb), .out9(jbe), .out10(ja), .out11(jae), .out12(decoder_1_out12), .out13(decoder_1_out13),
    .out14(decoder_1_out14), .out15(decoder_1_out15), .sel(opcode));
  and and_1 (memLoad, ld, ld);
  and and_2 (memSt, st, st);
  or or_3 (je, decoder_1_out12, decoder_1_out13, decoder_1_out14, decoder_1_out15);
  or or_4 (jump, jmp, jb, jbe, ja, jae, je);
  or or_5 (regWE, add, addi, \and , andi, ld);
  and and_3 (jmpRn, jump, jmp);
  and and_4 (jumpB, jump, jb);
  and and_5 (jumpBE, jump, jbe);
  and and_6 (jumpA, jump, ja);
  and and_7 (jumpAE, jump, jae);
  and and_8 (jumpE, jump, je);

  assign regSelect = jump;

  // Other names for the same wires on the sheet: cmp = Compare
endmodule

module datapath (
  input  [7:0] address,
  input  memStore,
  input  memLoad,
  input  [3:0] read_reg1,
  input  [3:0] read_reg2,
  input  [3:0] aluImmVal,
  input  [3:0] write_reg,
  input  aluImm,
  input  aluSlc,
  input  we,
  input  regClc,
  input  reset,
  output [15:0] dmOUT,
  output [15:0] src1,
  output [15:0] src2
);

  wire or_1_out, or_2_out;
  wire [11:0] bit_extender_2_out;
  wire [15:0] aluOut, bit_extender_1_out, multiplexer_1_out, multiplexer_2_out;

  assign bit_extender_1_out = {{8{1'b0}}, address};  // Bit_Extender bit_extender_1
  Multiplexer #(.width(16), .enable("false")) multiplexer_1 (
    .in0(src2), .in1(bit_extender_1_out), .out(multiplexer_1_out), .sel(or_1_out));
  or or_1 (or_1_out, memStore, memLoad);
  Multiplexer #(.width(16), .enable("false")) multiplexer_2 (
    .in0(aluOut), .in1(dmOUT), .out(multiplexer_2_out), .sel(or_2_out));
  or or_2 (or_2_out, memStore, memLoad);
  regFile REG (
    .read_register1(read_reg1), .read_register_2(read_reg2), .write_register(write_reg),
    .write_data(multiplexer_2_out), .we(we), .clc(regClc), .reset(reset), .source1(src1), .source2(src2));
  Bit_Extender #(.in_width(16), .out_width(12)) bit_extender_2 (.in(multiplexer_1_out), .out(bit_extender_2_out));
  RAM #(.addrWidth(12), .dataWidth(16), .bus("separate")) ram_1 (
    .addr(bit_extender_2_out), .din(src1), .data(dmOUT), .str(memStore), .ld(memLoad), .clr(1'b0));  // open: sel, clk
  alu ALU (.source1(src1), .source2(src2), .immediate(aluImmVal), .aluImm(aluImm), .aluSlc(aluSlc), .out(aluOut));

  // Other names for the same wires on the sheet: memSt = memStore

  // Notes on the sheet:
  //   A' YA 12 BİTLİK DEĞER
  //   D'YE 16 BİTLİK DEĞER
endmodule

module regFile (
  input  [3:0] read_register1,
  input  [3:0] read_register_2,
  input  [3:0] write_register,
  input  [15:0] write_data,
  input  we,
  input  clc,
  input  reset,
  output [15:0] source1,
  output [15:0] source2
);

  wire and_1_out, and_2_out, and_3_out, and_4_out, and_5_out, and_6_out, and_7_out, and_8_out, and_9_out,
       and_10_out, and_11_out, and_12_out, and_13_out, and_14_out, and_15_out, and_16_out, decoder_1_out0,
       decoder_1_out1, decoder_1_out2, decoder_1_out3, decoder_1_out4, decoder_1_out5, decoder_1_out6,
       decoder_1_out7, decoder_1_out8, decoder_1_out9, decoder_1_out10, decoder_1_out11, decoder_1_out12,
       decoder_1_out13, decoder_1_out14, decoder_1_out15;
  wire [15:0] register_1_q, register_2_q, register_3_q, register_4_q, register_5_q, register_6_q,
       register_7_q, register_8_q, register_9_q, register_10_q, register_11_q, register_12_q, register_13_q,
       register_14_q, register_15_q, register_16_q;

  Decoder #(.select(4), .enable("false")) decoder_1 (
    .out0(decoder_1_out0), .out1(decoder_1_out1), .out2(decoder_1_out2), .out3(decoder_1_out3),
    .out4(decoder_1_out4), .out5(decoder_1_out5), .out6(decoder_1_out6), .out7(decoder_1_out7),
    .out8(decoder_1_out8), .out9(decoder_1_out9), .out10(decoder_1_out10), .out11(decoder_1_out11),
    .out12(decoder_1_out12), .out13(decoder_1_out13), .out14(decoder_1_out14), .out15(decoder_1_out15),
    .sel(write_register));
  and and_1 (and_1_out, decoder_1_out0, we);
  and and_2 (and_2_out, decoder_1_out1, we);
  and and_3 (and_3_out, decoder_1_out2, we);
  and and_4 (and_4_out, decoder_1_out3, we);
  and and_5 (and_5_out, decoder_1_out4, we);
  and and_6 (and_6_out, decoder_1_out5, we);
  and and_7 (and_7_out, decoder_1_out6, we);
  and and_8 (and_8_out, decoder_1_out7, we);
  Register #(.width(16)) register_1 (.D(write_data), .en(and_1_out), .Q(register_1_q), .clk(clc), .clr(reset));
  Register #(.width(16)) register_2 (.D(write_data), .en(and_2_out), .Q(register_2_q), .clk(clc), .clr(reset));
  Register #(.width(16)) register_3 (.D(write_data), .en(and_3_out), .Q(register_3_q), .clk(clc), .clr(reset));
  Register #(.width(16)) register_4 (.D(write_data), .en(and_4_out), .Q(register_4_q), .clk(clc), .clr(reset));
  Register #(.width(16)) register_5 (.D(write_data), .en(and_5_out), .Q(register_5_q), .clk(clc), .clr(reset));
  Register #(.width(16)) register_6 (.D(write_data), .en(and_6_out), .Q(register_6_q), .clk(clc), .clr(reset));
  Register #(.width(16)) register_7 (.D(write_data), .en(and_7_out), .Q(register_7_q), .clk(clc), .clr(reset));
  Register #(.width(16)) register_8 (.D(write_data), .en(and_8_out), .Q(register_8_q), .clk(clc), .clr(reset));
  and and_9 (and_9_out, decoder_1_out8, we);
  and and_10 (and_10_out, decoder_1_out9, we);
  and and_11 (and_11_out, decoder_1_out10, we);
  and and_12 (and_12_out, decoder_1_out11, we);
  and and_13 (and_13_out, decoder_1_out12, we);
  and and_14 (and_14_out, decoder_1_out13, we);
  and and_15 (and_15_out, decoder_1_out14, we);
  and and_16 (and_16_out, decoder_1_out15, we);
  Register #(.width(16)) register_9 (.D(write_data), .en(and_9_out), .Q(register_9_q), .clk(clc), .clr(reset));
  Register #(.width(16)) register_10 (.D(write_data), .en(and_10_out), .Q(register_10_q), .clk(clc), .clr(reset));
  Register #(.width(16)) register_11 (.D(write_data), .en(and_11_out), .Q(register_11_q), .clk(clc), .clr(reset));
  Register #(.width(16)) register_12 (.D(write_data), .en(and_12_out), .Q(register_12_q), .clk(clc), .clr(reset));
  Register #(.width(16)) register_13 (.D(write_data), .en(and_13_out), .Q(register_13_q), .clk(clc), .clr(reset));
  Register #(.width(16)) register_14 (.D(write_data), .en(and_14_out), .Q(register_14_q), .clk(clc), .clr(reset));
  Register #(.width(16)) register_15 (.D(write_data), .en(and_15_out), .Q(register_15_q), .clk(clc), .clr(reset));
  Register #(.width(16)) register_16 (.D(write_data), .en(and_16_out), .Q(register_16_q), .clk(clc), .clr(reset));
  Multiplexer #(.select(4), .width(16), .enable("false")) multiplexer_1 (
    .in0(register_1_q), .in1(register_2_q), .in2(register_3_q), .in3(register_4_q), .in4(register_5_q),
    .in5(register_6_q), .in6(register_7_q), .in7(register_8_q), .in8(register_9_q), .in9(register_10_q),
    .in10(register_11_q), .in11(register_12_q), .in12(register_13_q), .in13(register_14_q),
    .in14(register_15_q), .in15(register_16_q), .out(source2), .sel(read_register_2));
  Multiplexer #(.select(4), .width(16), .enable("false")) multiplexer_2 (
    .in0(register_1_q), .in1(register_2_q), .in2(register_3_q), .in3(register_4_q), .in4(register_5_q),
    .in5(register_6_q), .in6(register_7_q), .in7(register_8_q), .in8(register_9_q), .in9(register_10_q),
    .in10(register_11_q), .in11(register_12_q), .in12(register_13_q), .in13(register_14_q),
    .in14(register_15_q), .in15(register_16_q), .out(source1), .sel(read_register1));
endmodule

module compare (
  input  [15:0] src1,
  input  [15:0] src2,
  output CF,
  output ZF
);

  wire or_1_out, or_2_out, or_3_out, or_4_out, or_5_out, or_6_out, or_7_out, or_8_out;
  wire [15:0] subtractor_1_out;

  Subtractor #(.width(16)) subtractor_1 (.a(src1), .b(src2), .out(subtractor_1_out), .bout(CF));  // open: bin
  or or_1 (or_1_out, subtractor_1_out[15], subtractor_1_out[14], subtractor_1_out[13]);
  or or_2 (or_2_out, subtractor_1_out[9], subtractor_1_out[8], subtractor_1_out[7]);
  or or_3 (or_3_out, subtractor_1_out[12], subtractor_1_out[11], subtractor_1_out[10]);
  or or_4 (or_4_out, or_1_out, or_3_out, or_2_out);
  or or_5 (or_5_out, or_4_out, or_8_out);
  not not_1 (ZF, or_5_out);
  or or_6 (or_6_out, subtractor_1_out[6], subtractor_1_out[5], subtractor_1_out[4]);
  or or_7 (or_7_out, subtractor_1_out[3], subtractor_1_out[2], subtractor_1_out[1], subtractor_1_out[0]);
  or or_8 (or_8_out, or_6_out, or_7_out);
endmodule

module alu (
  input  [15:0] source1,
  input  [15:0] source2,
  input  aluSlc,
  input  [3:0] immediate,
  input  aluImm,
  output [15:0] out
);

  wire adder_1_cout;
  wire [15:0] adder_1_out, and_1_out, multiplexer_1_out;

  Multiplexer #(.width(16), .enable("false")) multiplexer_1 (
    .in0(source2), .in1({{13{immediate[3]}}, immediate[2:0]}), .out(multiplexer_1_out), .sel(aluImm));
  Adder #(.width(16)) adder_1 (.a(source1), .b(multiplexer_1_out), .out(adder_1_out), .cin(1'b0), .cout(adder_1_cout));
  assign and_1_out = source1 & multiplexer_1_out;  // AND_Gate and_1, 16 bits wide
  Multiplexer #(.width(16), .enable("false")) multiplexer_2 (
    .in0(adder_1_out), .in1(and_1_out), .out(out), .sel(aluSlc));
  // also tied to GND on the sheet: adder_1_cout
endmodule

module IR (
  input  [15:0] in_1,
  input  clock,
  input  clear,
  output [11:0] location,
  output [7:0] address,
  output [3:0] treg,
  output [3:0] sreg,
  output [3:0] dreg,
  output [3:0] opcode
);

  Register #(.width(16)) register_1 (.D(in_1), .en(1'b1), .Q({opcode, dreg, address}), .clk(clock), .clr(clear));

  assign location = {dreg, address};
  assign sreg = address[7:4];
  assign treg = address[3:0];
endmodule
