// Logisim project project.circ as structural Verilog
module main (
);

  wire CLOCK, IMM, IRLD, LD, MUX, PC_plus_plus;
  wire [1:0] MUXL, MUXR, REGSEL;
  wire [3:0] ALUOP;
  wire [11:0] pc_1_dout;
  wire [15:0] ALUOUT, D, multiplexer_2_out, multiplexer_3_out, multiplexer_4_out, MUXOUT,
       register_bank_1_reg1, register_bank_1_reg2, register_bank_1_reg3, register_bank_1_reg4;

  PC pc_1 (.PC_plus_plus(PC_plus_plus), .CLK(CLOCK), .DOUT(pc_1_dout));
  Clock clock_1 (.out(CLOCK));
  ROM #(.addrWidth(12), .dataWidth(16)) rom_1 (.addr(pc_1_dout), .data(D));  // open: sel
  Multiplexer #(.width(16), .enable("false")) multiplexer_1 (.in0(ALUOUT), .in1(D), .out(MUXOUT), .sel(MUX));
  Control_Unit control_unit_1 (
    .CLK(CLOCK), .D_15_14(D[15:14]), .LD(LD), .MUX(MUX), .IRLD(IRLD), .PC_plus_plus(PC_plus_plus), .IMM(IMM));
  Register_Bank register_bank_1 (
    .DOUT(MUXOUT), .REG1(register_bank_1_reg1), .REG2(register_bank_1_reg2), .REG3(register_bank_1_reg3),
    .REG4(register_bank_1_reg4), .REGSE(REGSEL), .LD(LD), .CLK(CLOCK));
  Multiplexer #(.select(2), .width(16), .enable("false")) multiplexer_2 (
    .in0(register_bank_1_reg1), .in1(register_bank_1_reg2), .in2(register_bank_1_reg3),
    .in3(register_bank_1_reg4), .out(multiplexer_2_out), .sel(MUXL));
  IR ir_1 (.D_11_0(D[11:0]), .IRLD(IRLD), .CLK(CLOCK), .REGSEL(REGSEL), .MUXR(MUXR), .MUXL(MUXL), .ALUOP(ALUOP));
  Multiplexer #(.select(2), .width(16), .enable("false")) multiplexer_3 (
    .in0(register_bank_1_reg1), .in1(register_bank_1_reg2), .in2(register_bank_1_reg3),
    .in3(register_bank_1_reg4), .out(multiplexer_3_out), .sel(MUXR));
  Multiplexer #(.width(16), .enable("false")) multiplexer_4 (
    .in0(multiplexer_3_out), .in1(D), .out(multiplexer_4_out), .sel(IMM));
  ALU alu_1 (.A(multiplexer_2_out), .B(multiplexer_4_out), .ALUOUT(ALUOUT), .ALUOP(ALUOP));
  Hex_Digit_Display hex_digit_display_1 (.value(register_bank_1_reg1[15:12]));  // open: dp
  Hex_Digit_Display hex_digit_display_2 (.value(register_bank_1_reg1[7:4]));  // open: dp
  Hex_Digit_Display hex_digit_display_3 (.value(register_bank_1_reg1[11:8]));  // open: dp
  Hex_Digit_Display hex_digit_display_4 (.value(register_bank_1_reg1[3:0]));  // open: dp

  // Other names for the same wires on the sheet: D_11_0[11:0] = D[11:0]; D_15_14[1:0] = D[15:14]

  // Notes on the sheet:
  //   contents of rom_1 (hex, n*v repeats v):
  //   4000 6b c301 18 8809 4002 1b c283 2d 851a 8088 8700 4001 c c142 5f 8513 84c0
endmodule

module PC (
  input  PC_plus_plus,
  input  CLK,
  output [11:0] DOUT
);

  wire [11:0] adder_1_out;

  Adder #(.width(12)) adder_1 (.a(DOUT), .b(12'h1), .out(adder_1_out));  // open: cin, cout
  _12_bit_reg u_12_bit_reg_1 (.DATA(adder_1_out), .LOAD(PC_plus_plus), .CLK(CLK), .out_4(DOUT));
endmodule

// CONTROL
module Control_Unit (
  input  [1:0] D_15_14,
  input  CLK,
  output LD,
  output MUX,
  output IRLD,
  output PC_plus_plus,
  output IMM
);

  wire [1:0] multiplexer_1_out, n2_bit_reg_1_out;
  wire [5:5] rom_1_data;

  Multiplexer #(.width(2), .enable("false")) multiplexer_1 (
    .in0(D_15_14), .in1(2'b00), .out(multiplexer_1_out), .sel(rom_1_data[5]));
  _2_bit_reg u_2_bit_reg_1 (.DATA(multiplexer_1_out), .LOAD(1'b1), .CLK(CLK), .OUT(n2_bit_reg_1_out));
  ROM #(.addrWidth(2), .dataWidth(6)) rom_1 (
    .addr(n2_bit_reg_1_out), .data({rom_1_data[5], LD, MUX, IRLD, PC_plus_plus, IMM}));  // open: sel

  // Notes on the sheet:
  //   contents of rom_1 (hex, n*v repeats v):
  //   6 3a 30 37
endmodule

module IR (
  input  [11:0] D_11_0,
  input  IRLD,
  input  CLK,
  output [1:0] REGSEL,
  output [1:0] MUXR,
  output [1:0] MUXL,
  output [3:0] ALUOP
);

  wire [5:2] n12_bit_reg_1_out_4;

  _12_bit_reg u_12_bit_reg_1 (
    .DATA(D_11_0), .LOAD(IRLD), .CLK(CLK),
    .out_4({ALUOP, MUXL, n12_bit_reg_1_out_4[5], MUXR, n12_bit_reg_1_out_4[2], REGSEL}));
endmodule

module ALU (
  input  [15:0] A,
  input  [15:0] B,
  input  [3:0] ALUOP,
  output [15:0] ALUOUT
);

  wire [15:0] A_1, A_1_t, ADD, AND, NOT, OR, SUB, XOR;

  Adder #(.width(16)) adder_1 (.a(A), .b(B), .out(ADD));  // open: cin, cout
  Subtractor #(.width(16)) subtractor_1 (.a(A), .b(B), .out(SUB));  // open: bin, bout
  assign AND = A & B;  // AND_Gate and_1, 16 bits wide
  assign OR = A | B;  // OR_Gate or_1, 16 bits wide
  assign XOR = A ^ B;  // XOR_Gate xor_1, 16 bits wide
  assign NOT = ~B;  // NOT_Gate not_1, 16 bits wide
  Adder #(.width(16)) adder_2 (.a(B), .b(16'h1), .out(A_1));  // open: cin, cout
  Subtractor #(.width(16)) subtractor_2 (.a(B), .b(16'h1), .out(A_1_t));  // open: bin, bout
  Multiplexer #(.select(4), .width(16), .enable("false")) multiplexer_1 (
    .in0(ADD), .in1(SUB), .in2(AND), .in3(OR), .in4(XOR), .in5(NOT), .in6(A), .in7(A_1), .in8(A_1_t),
    .out(ALUOUT), .sel(ALUOP));  // open: in9, in10, in11, in12, in13, in14, in15
endmodule

// REGBANK
module Register_Bank (
  input  [15:0] DOUT,
  input  [1:0] REGSE,
  input  LD,
  input  CLK,
  output [15:0] REG1,
  output [15:0] REG2,
  output [15:0] REG3,
  output [15:0] REG4
);

  wire and_1_out, and_2_out, and_3_out, and_4_out, decoder_1_out0, decoder_1_out1, decoder_1_out2,
       decoder_1_out3;

  Decoder #(.select(2), .enable("false")) decoder_1 (
    .out0(decoder_1_out0), .out1(decoder_1_out1), .out2(decoder_1_out2), .out3(decoder_1_out3), .sel(REGSE));
  and and_1 (and_1_out, decoder_1_out0, LD);
  and and_2 (and_2_out, decoder_1_out1, LD);
  and and_3 (and_3_out, decoder_1_out2, LD);
  and and_4 (and_4_out, decoder_1_out3, LD);
  _16_bit_reg u_16_bit_reg_1 (.DATA(DOUT), .LOAD(and_1_out), .CLK(CLK), .OUT(REG1));
  _16_bit_reg u_16_bit_reg_2 (.DATA(DOUT), .LOAD(and_2_out), .CLK(CLK), .OUT(REG2));
  _16_bit_reg u_16_bit_reg_3 (.DATA(DOUT), .LOAD(and_3_out), .CLK(CLK), .OUT(REG3));
  _16_bit_reg u_16_bit_reg_4 (.DATA(DOUT), .LOAD(and_4_out), .CLK(CLK), .OUT(REG4));
endmodule

module _16_bit_reg (
  input  [15:0] DATA,
  input  LOAD,
  input  CLK,
  output [15:0] OUT
);

  _4_bit_reg u_4_bit_reg_1 (.DATA(DATA[3:0]), .LOAD(LOAD), .CLK(CLK), .OUT(OUT[3:0]));
  _4_bit_reg u_4_bit_reg_2 (.DATA(DATA[7:4]), .LOAD(LOAD), .CLK(CLK), .OUT(OUT[7:4]));
  _4_bit_reg u_4_bit_reg_3 (.DATA(DATA[11:8]), .LOAD(LOAD), .CLK(CLK), .OUT(OUT[11:8]));
  _4_bit_reg u_4_bit_reg_4 (.DATA(DATA[15:12]), .LOAD(LOAD), .CLK(CLK), .OUT(OUT[15:12]));
endmodule

module _4_bit_reg (
  input  [3:0] DATA,
  input  LOAD,
  input  CLK,
  output [3:0] OUT
);

  wire and_1_out, and_2_out, and_3_out, and_4_out, and_5_out, and_6_out, and_7_out, and_8_out, not_1_out,
       not_2_out, not_3_out, not_4_out;

  not not_1 (not_1_out, DATA[0]);
  not not_2 (not_2_out, DATA[1]);
  not not_3 (not_3_out, DATA[2]);
  not not_4 (not_4_out, DATA[3]);
  and and_1 (and_1_out, DATA[0], LOAD);
  and and_2 (and_2_out, not_1_out, LOAD);
  and and_3 (and_3_out, DATA[1], LOAD);
  and and_4 (and_4_out, not_2_out, LOAD);
  and and_5 (and_5_out, DATA[2], LOAD);
  and and_6 (and_6_out, not_3_out, LOAD);
  and and_7 (and_7_out, DATA[3], LOAD);
  and and_8 (and_8_out, not_4_out, LOAD);
  S_R_Flip_Flop s_r_ff_1 (.S(and_1_out), .clk(CLK), .R(and_2_out), .Q(OUT[0]));  // open: Qn, preset, reset, en
  S_R_Flip_Flop s_r_ff_2 (.S(and_3_out), .clk(CLK), .R(and_4_out), .Q(OUT[1]));  // open: Qn, preset, reset, en
  S_R_Flip_Flop s_r_ff_3 (.S(and_5_out), .clk(CLK), .R(and_6_out), .Q(OUT[2]));  // open: Qn, preset, reset, en
  S_R_Flip_Flop s_r_ff_4 (.S(and_7_out), .clk(CLK), .R(and_8_out), .Q(OUT[3]));  // open: Qn, preset, reset, en
endmodule

module _12_bit_reg (
  input  [11:0] DATA,
  input  LOAD,
  input  CLK,
  output [11:0] out_4
);

  _4_bit_reg u_4_bit_reg_1 (.DATA(DATA[3:0]), .LOAD(LOAD), .CLK(CLK), .OUT(out_4[3:0]));
  _4_bit_reg u_4_bit_reg_2 (.DATA(DATA[7:4]), .LOAD(LOAD), .CLK(CLK), .OUT(out_4[7:4]));
  _4_bit_reg u_4_bit_reg_3 (.DATA(DATA[11:8]), .LOAD(LOAD), .CLK(CLK), .OUT(out_4[11:8]));
endmodule

module _2_bit_reg (
  input  [1:0] DATA,
  input  LOAD,
  input  CLK,
  output [1:0] OUT
);

  wire and_1_out, and_2_out, and_3_out, and_4_out, not_1_out, not_2_out;

  not not_1 (not_1_out, DATA[0]);
  not not_2 (not_2_out, DATA[1]);
  and and_1 (and_1_out, DATA[0], LOAD);
  and and_2 (and_2_out, not_1_out, LOAD);
  and and_3 (and_3_out, DATA[1], LOAD);
  and and_4 (and_4_out, not_2_out, LOAD);
  S_R_Flip_Flop s_r_ff_1 (.S(and_1_out), .clk(CLK), .R(and_2_out), .Q(OUT[0]));  // open: Qn, preset, reset, en
  S_R_Flip_Flop s_r_ff_2 (.S(and_3_out), .clk(CLK), .R(and_4_out), .Q(OUT[1]));  // open: Qn, preset, reset, en
endmodule
