// Logisim project interrupt.circ as structural Verilog: 22 circuits, main circuit main
module Top_Module (
  input  [15:0] KEY1,
  input  [15:0] KEY2
);

  wire clock_1_out, READY_KEY1_out, READY_KEY2_out;
  wire [3:0] main_1_count_3_0, main_1_count_7_4, main_1_count_11_8, main_1_count_15_12, main_1_disp_3_0,
       main_1_disp_7_4, main_1_disp_11_8, main_1_disp_15_12;

  Button READY_KEY1 (.out(READY_KEY1_out));
  Button READY_KEY2 (.out(READY_KEY2_out));
  Hex_Digit_Display hex_digit_display_1 (.value(main_1_count_15_12));  // open: dp
  Hex_Digit_Display hex_digit_display_2 (.value(main_1_count_11_8));  // open: dp
  Hex_Digit_Display hex_digit_display_3 (.value(main_1_count_3_0));  // open: dp
  Hex_Digit_Display hex_digit_display_4 (.value(main_1_count_7_4));  // open: dp
  Clock clock_1 (.out(clock_1_out));
  main main_1 (
    .KEY_1(KEY1), .KEY_2(KEY2), .READY_2(READY_KEY2_out), .READY_1(READY_KEY1_out),
    .DISP_3_0(main_1_disp_3_0), .DISP_7_4(main_1_disp_7_4), .DISP_11_8(main_1_disp_11_8),
    .DISP_15_12(main_1_disp_15_12), .CLK(clock_1_out), .COUNT_3_0(main_1_count_3_0),
    .COUNT_7_4(main_1_count_7_4), .COUNT_11_8(main_1_count_11_8), .COUNT_15_12(main_1_count_15_12));
  Hex_Digit_Display hex_digit_display_5 (.value(main_1_disp_15_12));  // open: dp
  Hex_Digit_Display hex_digit_display_6 (.value(main_1_disp_11_8));  // open: dp
  Hex_Digit_Display hex_digit_display_7 (.value(main_1_disp_7_4));  // open: dp
  Hex_Digit_Display hex_digit_display_8 (.value(main_1_disp_3_0));  // open: dp

  // Notes on the sheet:
  //   TIMER OUTPUT
  //   KEYPAD OUTPUT
endmodule

// MAIN BOARD
module main (
  input  [15:0] KEY_1,
  input  [15:0] KEY_2,
  input  READY_2,
  input  READY_1,
  input  CLK,
  output [3:0] DISP_3_0,
  output [3:0] DISP_7_4,
  output [3:0] DISP_11_8,
  output [3:0] DISP_15_12,
  output [3:0] COUNT_3_0,
  output [3:0] COUNT_7_4,
  output [3:0] COUNT_11_8,
  output [3:0] COUNT_15_12
);

  wire A00, A02, ACK, and_5_out, and_6_out, and_7_out, B00, B00_out, B01, INT, INT_GLOB, INTACK, IRD,
       ISR_MEM, MEM, MEMWT;
  wire [2:0] priority_encoder_1_out;
  wire [15:0] Addres_Out_11_0, Data_Out_15_0, DEVNUM, DIN, KEY1_DIN, KEY2_DIN, MEM_DIN, MEM_ISR,
       multiplexer_1_out, PICOUT, TIMER_OUT;

  and and_1 (ISR_MEM, Addres_Out_11_0[11], Addres_Out_11_0[10]);
  Input input_1 (.KEY(KEY_1), .READY_BIT(READY_1), .ADDRESS(A00), .OUTPUT(KEY1_DIN), .ADDRESS_0(Addres_Out_11_0[0]));
  and and_2 (MEM, ~Addres_Out_11_0[11], ~Addres_Out_11_0[10]);  // AND_Gate
  and _400 (IRD, ~Addres_Out_11_0[11], Addres_Out_11_0[10], ~Addres_Out_11_0[9], ~Addres_Out_11_0[8], ~Addres_Out_11_0[7], ~Addres_Out_11_0[6], ~Addres_Out_11_0[5], ~Addres_Out_11_0[4], ~Addres_Out_11_0[3], ~Addres_Out_11_0[2], ~Addres_Out_11_0[1]);  // AND_Gate
  Output output_1 (.DATA_OUT(Data_Out_15_0), .LOAD(B00), .CLK(CLK), .REG({DISP_15_12, DISP_11_8, DISP_7_4, DISP_3_0}));
  and and_3 (B00, ~Addres_Out_11_0[0], B00_out);  // AND_Gate
  and and_4 (B01, B00_out, Addres_Out_11_0[0]);
  and u_B00 (B00_out, Addres_Out_11_0[11], ~Addres_Out_11_0[10], Addres_Out_11_0[9], Addres_Out_11_0[8], ~Addres_Out_11_0[7], ~Addres_Out_11_0[6], ~Addres_Out_11_0[5], ~Addres_Out_11_0[4], ~Addres_Out_11_0[3], ~Addres_Out_11_0[2], ~Addres_Out_11_0[1]);  // AND_Gate
  Output output_2 (.DATA_OUT(TIMER_OUT), .LOAD(B01), .CLK(CLK), .REG({COUNT_15_12, COUNT_11_8, COUNT_7_4, COUNT_3_0}));
  Input input_2 (.KEY(KEY_2), .READY_BIT(READY_2), .ADDRESS(A02), .OUTPUT(KEY2_DIN), .ADDRESS_0(Addres_Out_11_0[0]));
  and u_A02 (A02, Addres_Out_11_0[11], ~Addres_Out_11_0[10], Addres_Out_11_0[9], ~Addres_Out_11_0[8], ~Addres_Out_11_0[7], ~Addres_Out_11_0[6], ~Addres_Out_11_0[5], ~Addres_Out_11_0[4], ~Addres_Out_11_0[3], ~Addres_Out_11_0[2], Addres_Out_11_0[1]);  // AND_Gate
  and u_A00 (A00, Addres_Out_11_0[11], ~Addres_Out_11_0[10], Addres_Out_11_0[9], ~Addres_Out_11_0[8], ~Addres_Out_11_0[7], ~Addres_Out_11_0[6], ~Addres_Out_11_0[5], ~Addres_Out_11_0[4], ~Addres_Out_11_0[3], ~Addres_Out_11_0[2], ~Addres_Out_11_0[1]);  // AND_Gate
  and and_5 (and_5_out, IRD, MEMWT);
  PIC pic_1 (
    .VEC_IN(Data_Out_15_0), .INT_SIG(INT), .VECLD(and_5_out), .VEC_OUT(PICOUT), .CLOCK(CLK), .DEVNUM(DEVNUM),
    .INT_GLOBAL(INT_GLOB), .CLEAR(ACK), .ACK(INTACK));
  timer_interrupt timer_interrupt_1 (.CLOCK(CLK), .TIMER_OUTPUT(TIMER_OUT), .INT(INT), .ACK(ACK));
  Multiplexer #(.select(3), .width(16), .enable("false")) multiplexer_1 (
    .in0(MEM_DIN), .in1({16{1'b0}}), .in2(KEY1_DIN), .in3(PICOUT), .in4({16{1'b0}}), .in5(KEY2_DIN),
    .in6({16{1'b0}}), .in7(MEM_ISR), .out(multiplexer_1_out), .sel(priority_encoder_1_out));
  Priority_Encoder priority_encoder_1 (
    .in0(MEM), .in1(1'b0), .in2(A00), .in3(IRD), .in4(1'b0), .in5(A02), .in6(1'b0), .in7(ISR_MEM),
    .out(priority_encoder_1_out));  // open: en_in, gs, en_out
  // Probe on Data_Out_15_0
  // Probe on nothing
  // Probe on priority_encoder_1_out
  Multiplexer #(.width(16), .enable("false")) multiplexer_2 (
    .in0(multiplexer_1_out), .in1(DEVNUM), .out(DIN), .sel(INTACK));
  and and_6 (and_6_out, MEM, MEMWT);
  and and_7 (and_7_out, ISR_MEM, MEMWT);
  // Probe on DIN
  RAM #(.addrWidth(16), .dataWidth(16), .bus("separate")) ram_1 (
    .addr(Addres_Out_11_0), .din(Data_Out_15_0), .data(MEM_ISR), .str(and_7_out), .clk(CLK));  // open: sel, ld, clr
  CPU cpu_1 (
    .ADDRES_OUT(Addres_Out_11_0), .MEMLD(MEMWT), .DATA_OUT(Data_Out_15_0), .DIN(DIN), .CLK(CLK),
    .INT(INT_GLOB), .INTACK(INTACK));
  RAM #(.addrWidth(16), .dataWidth(16), .bus("separate")) ram_2 (
    .addr(Addres_Out_11_0), .din(Data_Out_15_0), .data(MEM_DIN), .str(and_6_out), .clk(CLK));  // open: sel, ld, clr

  // Other names for the same wires on the sheet: Address_0 = Addres_Out_11_0[0];
  //   Address_Out_1_0[1:0] = Addres_Out_11_0[1:0]; CLOCK = CLK

  // Notes on the sheet:
  //   KEY_1: pull=up
  //   KEY_2: pull=up
endmodule

// INPUT
module Input (
  input  [15:0] KEY,
  input  READY_BIT,
  input  ADDRESS,
  input  ADDRESS_0,
  output [15:0] OUTPUT
);

  wire and_1_out;
  wire [0:0] ready_key_reg_1_out;
  wire [15:0] KEY_REG_out;

  ready_key_reg ready_key_reg_1 (.CLK(READY_BIT), .OUT(ready_key_reg_1_out[0]), .RESET(and_1_out));
  and and_1 (and_1_out, ADDRESS, ~ADDRESS_0);  // AND_Gate
  // Probe on KEY_REG_out
  _16_bit_reg KEY_REG (.DATA(KEY), .LOAD(1'b1), .CLK(ready_key_reg_1_out[0]), .OUT(KEY_REG_out));
  Multiplexer #(.width(16), .enable("false")) multiplexer_1 (
    .in0(KEY_REG_out), .in1({{15{1'b0}}, ready_key_reg_1_out[0]}), .out(OUTPUT), .sel(ADDRESS_0));

  // Notes on the sheet:
  //   KEY: pull=up
endmodule

module ready_key_reg (
  input  CLK,
  input  RESET,
  output OUT
);

  S_R_Flip_Flop s_r_ff_1 (.S(1'b1), .clk(CLK), .R(1'b0), .Q(OUT), .reset(RESET));  // open: Qn, preset, en
endmodule

// OUTPUT
module Output (
  input  [15:0] DATA_OUT,
  input  LOAD,
  input  CLK,
  output [15:0] REG
);

  _16_bit_reg u_16_bit_reg_1 (.DATA(DATA_OUT), .LOAD(LOAD), .CLK(CLK), .OUT(REG));
endmodule

// TIMER
module timer_interrupt (
  input  CLOCK,
  input  ACK,
  output [15:0] TIMER_OUTPUT,
  output INT
);

  wire [15:0] adder_1_out, adder_2_out, n16_bit_reg_1_out;

  // Probe on adder_1_out
  _16_bit_reg u_16_bit_reg_1 (.DATA(adder_1_out), .LOAD(1'b1), .CLK(CLOCK), .OUT(n16_bit_reg_1_out));
  Adder #(.width(16)) adder_1 (.a(16'h1), .b(n16_bit_reg_1_out), .out(adder_1_out));  // open: cin, cout
  S_R_Flip_Flop s_r_ff_1 (
    .S(n16_bit_reg_1_out[6]), .clk(CLOCK), .R(1'b0), .Q(INT), .preset(1'b0), .reset(ACK));  // open: Qn, en
  _16_bit_reg u_16_bit_reg_2 (.DATA(adder_2_out), .LOAD(1'b1), .CLK(n16_bit_reg_1_out[6]), .OUT(TIMER_OUTPUT));
  Adder #(.width(16)) adder_2 (.a(16'h1), .b(TIMER_OUTPUT), .out(adder_2_out));  // open: cin, cout
endmodule

module PIC (
  input  [15:0] VEC_IN,
  input  ACK,
  input  VECLD,
  input  CLOCK,
  input  INT_SIG,
  output CLEAR,
  output [15:0] VEC_OUT,
  output INT_GLOBAL,
  output [15:0] DEVNUM
);

  wire priority_encoder_1_en_out, priority_encoder_1_out, s_r_ff_1_q;

  _16_bit_reg u_16_bit_reg_1 (.DATA(VEC_IN), .LOAD(VECLD), .CLK(CLOCK), .OUT(VEC_OUT));
  not not_1 (INT_GLOBAL, priority_encoder_1_en_out);
  Priority_Encoder #(.select(1)) priority_encoder_1 (
    .in0(INT_SIG), .in1(INT_SIG), .out(priority_encoder_1_out), .en_out(priority_encoder_1_en_out));  // open: gs, en_in
  S_R_Flip_Flop #(.trigger("high")) s_r_ff_1 (
    .S(INT_GLOBAL), .clk(priority_encoder_1_out), .R(priority_encoder_1_en_out), .Q(s_r_ff_1_q));  // open: Qn, preset, reset, en
  and and_1 (CLEAR, s_r_ff_1_q, ACK);
  // Probe on s_r_ff_1_q
  assign DEVNUM = {{15{1'b0}}, s_r_ff_1_q};  // Bit_Extender bit_extender_1
endmodule

module CPU (
  input  [15:0] DIN,
  input  INT,
  input  CLK,
  output [15:0] ADDRES_OUT,
  output MEMLD,
  output [15:0] DATA_OUT,
  output INTACK
);

  wire CLI, FLAGLD, INT_FLAG, INT_LOAD, IRLD, MUX, PCINC, PCLOAD, PCMUX, REGLD, SP_minus_minus, SP_plus_plus,
       STI, ZF, ZFLD;
  wire [1:0] ARMUX, DATAMUX;
  wire [2:0] REGSE, SRCL, SRCR;
  wire [5:0] ALUOP;
  wire [11:0] IR;
  wire [15:0] adder_1_out, adder_2_out, ALUOUT, bit_extender_1_out, DOUT, multiplexer_1_out,
       multiplexer_4_out, PC_ADDR, REG6, REG_ADDR, regbank_1_reg0, regbank_1_reg1, regbank_1_reg2,
       regbank_1_reg3, regbank_1_reg4, regbank_1_reg5, SP, VEC_OUT;

  assign bit_extender_1_out = {{4{IR[11]}}, IR};  // Bit_Extender bit_extender_1
  // Probe on multiplexer_1_out
  Multiplexer #(.width(16), .enable("false")) multiplexer_1 (
    .in0(adder_1_out), .in1(DIN), .out(multiplexer_1_out), .sel(PCMUX));
  Adder #(.width(16)) adder_1 (.a(PC_ADDR), .b(bit_extender_1_out), .out(adder_1_out));  // open: cin, cout
  // Probe on nothing
  Multiplexer #(.select(2), .width(16), .enable("false")) multiplexer_2 (
    .in0(PC_ADDR), .in1(REG_ADDR), .in2(SP), .in3(VEC_OUT), .out(ADDRES_OUT), .sel(ARMUX));
  PC pc_1 (.ADDRESS_IN(multiplexer_1_out), .ADDR_OUT(PC_ADDR), .PCLOAD(PCLOAD), .PCINC(PCINC), .CLK(CLK));
  Multiplexer #(.select(2), .width(16), .enable("false")) multiplexer_3 (
    .in0(DOUT), .in1(PC_ADDR), .in2({REG6[15:2], INT_FLAG, REG6[0]}), .out(DATA_OUT), .sel(DATAMUX));  // open: in3
  CONTROL_UNIT control_unit_1 (
    .OPCODE(DIN[15:12]), .ZF(ZF), .INTLD(INT_LOAD), .INTACK(INTACK), .INT(INT), .CLI(CLI),
    .INT_FLAG(INT_FLAG), .STI(STI), .ZFLD(ZFLD), .SP_minus_minus(SP_minus_minus),
    .SP_plus_plus(SP_plus_plus), .CLOCK(CLK), .PCMUX(PCMUX), .REGLD(REGLD), .PCLOAD(PCLOAD), .PCINC(PCINC),
    .DATAMUX(DATAMUX), .MUX(MUX), .MEMLD(MEMLD), .IRLD(IRLD), .ARMUX(ARMUX), .FLAGLD(FLAGLD));
  Adder #(.width(16)) adder_2 (.a(DIN), .b(16'h400), .out(adder_2_out), .cin(1'b0));  // open: cout
  // Probe on multiplexer_4_out
  _16_bit_reg u_16_bit_reg_1 (.DATA(adder_2_out), .LOAD(INT_LOAD), .CLK(CLK), .OUT(VEC_OUT));
  Multiplexer #(.width(16), .enable("false")) multiplexer_4 (
    .in0(ALUOUT), .in1(DIN), .out(multiplexer_4_out), .sel(MUX));
  REGBANK regbank_1 (
    .DOUT(multiplexer_4_out), .REG0(regbank_1_reg0), .REG1(regbank_1_reg1), .REG2(regbank_1_reg2),
    .REG3(regbank_1_reg3), .REG4(regbank_1_reg4), .REG5(regbank_1_reg5), .REGSE(REGSE),
    .REG6({REG6[15:2], INT_FLAG, REG6[0]}), .STI(STI), .REG7(SP), .CLI(CLI), .ZFLD(ZFLD), .ZF(ZF),
    .REGLD(REGLD), .SP_minus_minus(SP_minus_minus), .SP_plus_plus(SP_plus_plus), .CLK(CLK), .FLAG_LOAD(FLAGLD));
  Multiplexer #(.select(3), .width(16), .enable("false")) multiplexer_5 (
    .in0(regbank_1_reg0), .in1(regbank_1_reg1), .in2(regbank_1_reg2), .in3(regbank_1_reg3),
    .in4(regbank_1_reg4), .in5(regbank_1_reg5), .in6({REG6[15:2], INT_FLAG, REG6[0]}), .in7(SP), .out(DOUT),
    .sel(SRCL));
  Multiplexer #(.select(3), .width(16), .enable("false")) multiplexer_6 (
    .in0(regbank_1_reg0), .in1(regbank_1_reg1), .in2(regbank_1_reg2), .in3(regbank_1_reg3),
    .in4(regbank_1_reg4), .in5(regbank_1_reg5), .in6({REG6[15:2], INT_FLAG, REG6[0]}), .in7(SP),
    .out(REG_ADDR), .sel(SRCR));
  ALU alu_1 (.ALUSELECT(ALUOP), .ALUOUT(ALUOUT), .SRCL(DOUT), .SRCR(REG_ADDR), .ZFLD(ZFLD), .CLOCK(CLK), .ZF(ZF));
  IR ir_1 (
    .DIN(DIN[11:0]), .REGSELECT(REGSE), .SRCR(SRCR), .SRCL(SRCL), .ALUOP(ALUOP), .IRLD(IRLD), .CLOCK(CLK),
    .IR(IR));

  // Other names for the same wires on the sheet: D_11_0[11:0] = DIN[11:0]; OPCODE[3:0] = DIN[15:12];
  //   REG6[1] = INT_FLAG
endmodule

module CONTROL_UNIT (
  input  [3:0] OPCODE,
  input  ZF,
  input  INT,
  input  INT_FLAG,
  input  CLOCK,
  output INTLD,
  output INTACK,
  output CLI,
  output STI,
  output ZFLD,
  output SP_minus_minus,
  output SP_plus_plus,
  output PCMUX,
  output REGLD,
  output PCLOAD,
  output PCINC,
  output [1:0] DATAMUX,
  output MUX,
  output MEMLD,
  output IRLD,
  output [1:0] ARMUX,
  output FLAGLD
);

  wire and_2_out, not_1_out, not_2_out, not_3_out, ZERO;
  wire [1:1] and_1_out;
  wire [3:0] multiplexer_1_out;
  wire [4:0] multiplexer_2_out, multiplexer_3_out, n5_bit_reg_1_out, rom_1_data;
  wire [4:4] undriven;
  wire [24:24] rom_1_data_2;

  and and_1 (and_1_out[1], not_1_out, not_2_out, OPCODE[2], not_3_out);
  not not_1 (not_1_out, OPCODE[0]);
  not not_2 (not_2_out, OPCODE[1]);
  not not_3 (not_3_out, OPCODE[3]);
  Multiplexer #(.select(2), .width(4), .enable("false")) multiplexer_1 (
    .in0(OPCODE), .in1(OPCODE), .in2(4'b0000), .in3(4'b0101), .out(multiplexer_1_out),
    .sel({and_1_out[1], ZF}));
  Multiplexer #(.width(5), .enable("false")) multiplexer_2 (
    .in0(rom_1_data), .in1({undriven[4], multiplexer_1_out}), .out(multiplexer_2_out), .sel(rom_1_data_2[24]));
  and and_2 (and_2_out, INT, INT_FLAG, ZERO);
  Multiplexer #(.width(5), .enable("false")) multiplexer_3 (
    .in0(multiplexer_2_out), .in1(5'b10011), .out(multiplexer_3_out), .sel(and_2_out));
  _5_bit_reg u_5_bit_reg_1 (.DATA(multiplexer_3_out), .LOAD(1'b1), .CLK(CLOCK), .OUT(n5_bit_reg_1_out));
  // Probe on nothing
  ROM #(.addrWidth(5), .dataWidth(25)) rom_1 (
    .addr(n5_bit_reg_1_out),
    .data({rom_1_data_2[24], FLAGLD, ARMUX, IRLD, MEMLD, MUX, DATAMUX, PCINC, PCLOAD, REGLD, PCMUX, SP_plus_plus, SP_minus_minus, ZFLD, STI, CLI, INTACK, INTLD, rom_1_data}));  // open: sel
  // Probe on rom_1_data
  and and_3 (ZERO, ~rom_1_data[0], ~rom_1_data[1], ~rom_1_data[2], ~rom_1_data[3], ~rom_1_data[4]);  // AND_Gate

  // Notes on the sheet:
  //   contents of rom_1 (hex, n*v repeats v):
  //   110801f 4a000 242000 280000 0 4000 0 2200 480400 80f 494400 810 80 100 811 442000 405000 405812
  //   c42000 4a0494 490475 605000
endmodule

// REG BANK
module REGBANK (
  input  [15:0] DOUT,
  input  FLAG_LOAD,
  input  [2:0] REGSE,
  input  STI,
  input  REGLD,
  input  SP_minus_minus,
  input  SP_plus_plus,
  input  CLK,
  input  CLI,
  input  ZFLD,
  input  ZF,
  output [15:0] REG0,
  output [15:0] REG1,
  output [15:0] REG2,
  output [15:0] REG3,
  output [15:0] REG4,
  output [15:0] REG5,
  output [15:0] REG6,
  output [15:0] REG7
);

  wire and_1_out, and_2_out, and_3_out, and_4_out, and_5_out, and_6_out, and_7_out, and_8_out,
       decoder_1_out0, decoder_1_out1, decoder_1_out2, decoder_1_out3, decoder_1_out4, decoder_1_out5,
       decoder_1_out6, decoder_1_out7;
  wire [2:0] multiplexer_1_out;

  Decoder #(.select(3), .enable("false")) decoder_1 (
    .out0(decoder_1_out0), .out1(decoder_1_out1), .out2(decoder_1_out2), .out3(decoder_1_out3),
    .out4(decoder_1_out4), .out5(decoder_1_out5), .out6(decoder_1_out6), .out7(decoder_1_out7),
    .sel(multiplexer_1_out));
  Multiplexer #(.width(3), .enable("false")) multiplexer_1 (
    .in0(REGSE), .in1(3'b110), .out(multiplexer_1_out), .sel(FLAG_LOAD));
  and and_1 (and_1_out, decoder_1_out0, REGLD);
  and and_2 (and_2_out, decoder_1_out1, REGLD);
  and and_3 (and_3_out, decoder_1_out2, REGLD);
  and and_4 (and_4_out, decoder_1_out3, REGLD);
  and and_5 (and_5_out, decoder_1_out4, REGLD);
  and and_6 (and_6_out, decoder_1_out5, REGLD);
  and and_7 (and_7_out, decoder_1_out6, REGLD);
  and and_8 (and_8_out, decoder_1_out7, REGLD);
  _16_bit_reg u_16_bit_reg_1 (.DATA(DOUT), .LOAD(and_1_out), .CLK(CLK), .OUT(REG0));
  _16_bit_reg u_16_bit_reg_2 (.DATA(DOUT), .LOAD(and_2_out), .CLK(CLK), .OUT(REG1));
  _16_bit_reg u_16_bit_reg_3 (.DATA(DOUT), .LOAD(and_3_out), .CLK(CLK), .OUT(REG2));
  _16_bit_reg u_16_bit_reg_4 (.DATA(DOUT), .LOAD(and_4_out), .CLK(CLK), .OUT(REG3));
  _16_bit_reg u_16_bit_reg_5 (.DATA(DOUT), .LOAD(and_5_out), .CLK(CLK), .OUT(REG4));
  _16_bit_reg u_16_bit_reg_6 (.DATA(DOUT), .LOAD(and_6_out), .CLK(CLK), .OUT(REG5));
  flag_reg flag_reg_1 (
    .DIN(DOUT), .FLAG_LOAD(and_7_out), .ZF(ZFLD), .ZFLD(ZF), .OUT(REG6), .STI(STI), .CLI(CLI), .CLK(CLK));
  SP_REG sp_reg_1 (.DIN(DOUT), .DOUT(REG7), .DEC(SP_minus_minus), .INC(SP_plus_plus), .LOAD(and_8_out), .CLOCK(CLK));
endmodule

module ALU (
  input  [15:0] SRCL,
  input  [15:0] SRCR,
  input  [5:0] ALUSELECT,
  input  CLOCK,
  input  ZFLD,
  output [15:0] ALUOUT,
  output ZF
);

  wire not_2_out, not_3_out, not_4_out, not_5_out, not_6_out, not_7_out, not_8_out, not_9_out, not_10_out,
       not_11_out, not_12_out, not_13_out, not_14_out, not_15_out, not_16_out, not_17_out, ZF_out;
  wire [15:0] adder_1_out, adder_2_out, and_1_out, multiplexer_1_out, not_1_out, or_1_out, subtractor_1_out,
       subtractor_2_out, xor_1_out;

  // Probe on nothing
  Adder #(.width(16)) adder_1 (.a(SRCR), .b(SRCL), .out(adder_1_out));  // open: cin, cout
  Subtractor #(.width(16)) subtractor_1 (.a(SRCR), .b(SRCL), .out(subtractor_1_out));  // open: bin, bout
  assign and_1_out = SRCR & SRCL;  // AND_Gate and_1, 16 bits wide
  assign or_1_out = SRCR | SRCL;  // OR_Gate or_1, 16 bits wide
  assign xor_1_out = SRCR ^ SRCL;  // XOR_Gate xor_1, 16 bits wide
  assign not_1_out = ~SRCR;  // NOT_Gate not_1, 16 bits wide
  Adder #(.width(16)) adder_2 (.a(SRCR), .b(16'h1), .out(adder_2_out));  // open: cin, cout
  Subtractor #(.width(16)) subtractor_2 (.a(SRCR), .b(16'h1), .out(subtractor_2_out));  // open: bin, bout
  Multiplexer #(.select(3), .width(16), .enable("false")) multiplexer_1 (
    .in0(not_1_out), .in1(SRCR), .in2(adder_2_out), .in3(subtractor_2_out), .out(multiplexer_1_out),
    .sel(ALUSELECT[2:0]));  // open: in4, in5, in6, in7
  Multiplexer #(.select(3), .width(16), .enable("false")) multiplexer_2 (
    .in0(adder_1_out), .in1(subtractor_1_out), .in2(and_1_out), .in3(or_1_out), .in4(xor_1_out),
    .in7(multiplexer_1_out), .out(ALUOUT), .sel(ALUSELECT[5:3]));  // open: in5, in6
  not not_2 (not_2_out, ALUOUT[14]);
  not not_3 (not_3_out, ALUOUT[15]);
  not not_4 (not_4_out, ALUOUT[13]);
  not not_5 (not_5_out, ALUOUT[10]);
  not not_6 (not_6_out, ALUOUT[12]);
  not not_7 (not_7_out, ALUOUT[11]);
  not not_8 (not_8_out, ALUOUT[8]);
  not not_9 (not_9_out, ALUOUT[7]);
  not not_10 (not_10_out, ALUOUT[9]);
  not not_11 (not_11_out, ALUOUT[6]);
  and u_ZF (ZF_out, not_3_out, not_2_out, not_4_out, not_6_out, not_7_out, not_5_out, not_10_out, not_8_out, not_9_out, not_11_out, not_15_out, not_13_out, not_12_out, not_14_out, not_17_out, not_16_out);
  _1_bit_reg u_1_bit_reg_1 (.DATA(ZF_out), .OUT(ZF), .LOAD(ZFLD), .CLK(CLOCK));
  not not_12 (not_12_out, ALUOUT[3]);
  not not_13 (not_13_out, ALUOUT[4]);
  not not_14 (not_14_out, ALUOUT[2]);
  not not_15 (not_15_out, ALUOUT[5]);
  not not_16 (not_16_out, ALUOUT[0]);
  not not_17 (not_17_out, ALUOUT[1]);
endmodule

module PC (
  input  [15:0] ADDRESS_IN,
  input  PCLOAD,
  input  PCINC,
  input  CLK,
  output [15:0] ADDR_OUT
);

  wire or_1_out;
  wire [15:0] adder_1_out, multiplexer_1_out;

  Adder #(.width(16)) adder_1 (.a(ADDR_OUT), .b(16'h1), .out(adder_1_out));  // open: cin, cout
  Multiplexer #(.width(16), .enable("false")) multiplexer_1 (
    .in0(adder_1_out), .in1(ADDRESS_IN), .out(multiplexer_1_out), .sel(PCLOAD));
  or or_1 (or_1_out, PCLOAD, PCINC);
  _16_bit_reg u_16_bit_reg_1 (.DATA(multiplexer_1_out), .LOAD(or_1_out), .CLK(CLK), .OUT(ADDR_OUT));
endmodule

module IR (
  input  [11:0] DIN,
  input  IRLD,
  input  CLOCK,
  output [11:0] IR,
  output [2:0] REGSELECT,
  output [2:0] SRCR,
  output [2:0] SRCL,
  output [5:0] ALUOP
);

  _12_bit_reg u_12_bit_reg_1 (.DATA(DIN), .LOAD(IRLD), .CLK(CLOCK), .out_4({ALUOP, IR[5:0]}));

  assign IR[11:6] = ALUOP;
  assign REGSELECT = IR[2:0];
  assign SRCL = ALUOP[2:0];
  assign SRCR = IR[5:3];
endmodule

module flag_reg (
  input  ZF,
  input  STI,
  input  CLI,
  input  ZFLD,
  input  [15:0] DIN,
  input  CLK,
  input  FLAG_LOAD,
  output [15:0] OUT
);

  wire and_1_out, and_2_out, and_3_out, and_4_out, or_1_out, or_2_out, or_3_out, or_4_out;

  and and_1 (and_1_out, STI, ~CLI);  // AND_Gate
  and and_2 (and_2_out, FLAG_LOAD, DIN[1]);
  or or_1 (or_1_out, and_1_out, and_2_out);
  or or_2 (or_2_out, STI, FLAG_LOAD, CLI);
  // Probe on OUT[1]
  _1_bit_reg IF (.DATA(or_1_out), .OUT(OUT[1]), .LOAD(or_2_out), .CLK(CLK));
  and and_3 (and_3_out, FLAG_LOAD, DIN[0]);
  and and_4 (and_4_out, ZF, ZFLD);
  or or_3 (or_3_out, and_4_out, and_3_out);
  or or_4 (or_4_out, FLAG_LOAD, ZFLD);
  _1_bit_reg u_ZF (.DATA(or_3_out), .OUT(OUT[0]), .LOAD(or_4_out), .CLK(CLK));

  assign OUT[15:2] = {14{1'b0}};

  // Other names for the same wires on the sheet: DIN_0 = DIN[0]; DIN_1 = DIN[1]; flgload = FLAG_LOAD; ZF_t = OUT[0];
  //   IF = OUT[1]
endmodule

// SP
module SP_REG (
  input  [15:0] DIN,
  input  DEC,
  input  INC,
  input  LOAD,
  input  CLOCK,
  output [15:0] DOUT
);

  wire or_1_out;
  wire [15:0] adder_1_out, multiplexer_1_out, subtractor_1_out;

  Multiplexer #(.select(2), .width(16), .enable("false")) multiplexer_1 (
    .in0(DIN), .in1(adder_1_out), .in2(subtractor_1_out), .out(multiplexer_1_out), .sel({DEC, INC}));  // open: in3
  or or_1 (or_1_out, INC, DEC, LOAD);
  _16_bit_reg u_16_bit_reg_1 (.DATA(multiplexer_1_out), .LOAD(or_1_out), .CLK(CLOCK), .OUT(DOUT));
  Adder #(.width(16)) adder_1 (.a(DOUT), .b(16'h1), .out(adder_1_out));  // open: cin, cout
  Subtractor #(.width(16)) subtractor_1 (.a(DOUT), .b(16'h1), .out(subtractor_1_out));  // open: bin, bout
endmodule

module _16_bit_reg (
  input  [15:0] DATA,
  input  LOAD,
  input  CLK,
  output [15:0] OUT
);

  _4_bit_reg u_4_bit_reg_1 (.DATA(DATA[3:0]), .LOAD(LOAD), .CLK(CLK), .OUT(OUT[3:0]));
  _4_bit_reg u_4_bit_reg_2 (.DATA(DATA[7:4]), .LOAD(LOAD), .CLK(CLK), .OUT(OUT[7:4]));
  _4_bit_reg u_4_bit_reg_3 (.DATA(DATA[11:8]), .LOAD(LOAD), .CLK(CLK), .OUT(OUT[11:8]));
  _4_bit_reg u_4_bit_reg_4 (.DATA(DATA[15:12]), .LOAD(LOAD), .CLK(CLK), .OUT(OUT[15:12]));
endmodule

module _12_bit_reg (
  input  [11:0] DATA,
  input  LOAD,
  input  CLK,
  output [11:0] out_4
);

  _4_bit_reg u_4_bit_reg_1 (.DATA(DATA[3:0]), .LOAD(LOAD), .CLK(CLK), .OUT(out_4[3:0]));
  _4_bit_reg u_4_bit_reg_2 (.DATA(DATA[7:4]), .LOAD(LOAD), .CLK(CLK), .OUT(out_4[7:4]));
  _4_bit_reg u_4_bit_reg_3 (.DATA(DATA[11:8]), .LOAD(LOAD), .CLK(CLK), .OUT(out_4[11:8]));
endmodule

module _5_bit_reg (
  input  [4:0] DATA,
  input  LOAD,
  input  CLK,
  output [4:0] OUT
);

  wire and_1_out, and_2_out, and_3_out, and_4_out, and_5_out, and_6_out, and_7_out, and_8_out, and_9_out,
       and_10_out, not_1_out, not_2_out, not_3_out, not_4_out, not_5_out;

  not not_1 (not_1_out, DATA[0]);
  not not_2 (not_2_out, DATA[1]);
  not not_3 (not_3_out, DATA[2]);
  not not_4 (not_4_out, DATA[3]);
  not not_5 (not_5_out, DATA[4]);
  and and_1 (and_1_out, DATA[0], LOAD);
  and and_2 (and_2_out, not_1_out, LOAD);
  and and_3 (and_3_out, DATA[1], LOAD);
  and and_4 (and_4_out, not_2_out, LOAD);
  and and_5 (and_5_out, DATA[2], LOAD);
  and and_6 (and_6_out, not_3_out, LOAD);
  and and_7 (and_7_out, DATA[3], LOAD);
  and and_8 (and_8_out, not_4_out, LOAD);
  and and_9 (and_9_out, DATA[4], LOAD);
  and and_10 (and_10_out, not_5_out, LOAD);
  S_R_Flip_Flop s_r_ff_1 (.S(and_1_out), .clk(CLK), .R(and_2_out), .Q(OUT[0]));  // open: Qn, preset, reset, en
  S_R_Flip_Flop s_r_ff_2 (.S(and_3_out), .clk(CLK), .R(and_4_out), .Q(OUT[1]));  // open: Qn, preset, reset, en
  S_R_Flip_Flop s_r_ff_3 (.S(and_5_out), .clk(CLK), .R(and_6_out), .Q(OUT[2]));  // open: Qn, preset, reset, en
  S_R_Flip_Flop s_r_ff_4 (.S(and_7_out), .clk(CLK), .R(and_8_out), .Q(OUT[3]));  // open: Qn, preset, reset, en
  S_R_Flip_Flop s_r_ff_5 (.S(and_9_out), .clk(CLK), .R(and_10_out), .Q(OUT[4]));  // open: Qn, preset, reset, en
endmodule

module _4_bit_reg (
  input  [3:0] DATA,
  input  LOAD,
  input  CLK,
  output [3:0] OUT
);

  wire and_1_out, and_2_out, and_3_out, and_4_out, and_5_out, and_6_out, and_7_out, and_8_out, not_1_out,
       not_2_out, not_3_out, not_4_out;

  not not_1 (not_1_out, DATA[0]);
  not not_2 (not_2_out, DATA[1]);
  not not_3 (not_3_out, DATA[2]);
  not not_4 (not_4_out, DATA[3]);
  and and_1 (and_1_out, DATA[0], LOAD);
  and and_2 (and_2_out, not_1_out, LOAD);
  and and_3 (and_3_out, DATA[1], LOAD);
  and and_4 (and_4_out, not_2_out, LOAD);
  and and_5 (and_5_out, DATA[2], LOAD);
  and and_6 (and_6_out, not_3_out, LOAD);
  and and_7 (and_7_out, DATA[3], LOAD);
  and and_8 (and_8_out, not_4_out, LOAD);
  S_R_Flip_Flop s_r_ff_1 (.S(and_1_out), .clk(CLK), .R(and_2_out), .Q(OUT[0]));  // open: Qn, preset, reset, en
  S_R_Flip_Flop s_r_ff_2 (.S(and_3_out), .clk(CLK), .R(and_4_out), .Q(OUT[1]));  // open: Qn, preset, reset, en
  S_R_Flip_Flop s_r_ff_3 (.S(and_5_out), .clk(CLK), .R(and_6_out), .Q(OUT[2]));  // open: Qn, preset, reset, en
  S_R_Flip_Flop s_r_ff_4 (.S(and_7_out), .clk(CLK), .R(and_8_out), .Q(OUT[3]));  // open: Qn, preset, reset, en
endmodule

module _2_bit_reg (
  input  [1:0] DATA,
  input  LOAD,
  input  CLK,
  output [1:0] OUT
);

  wire and_1_out, and_2_out, and_3_out, and_4_out, not_1_out, not_2_out;

  not not_1 (not_1_out, DATA[0]);
  not not_2 (not_2_out, DATA[1]);
  and and_1 (and_1_out, DATA[0], LOAD);
  and and_2 (and_2_out, not_1_out, LOAD);
  and and_3 (and_3_out, DATA[1], LOAD);
  and and_4 (and_4_out, not_2_out, LOAD);
  S_R_Flip_Flop s_r_ff_1 (.S(and_1_out), .clk(CLK), .R(and_2_out), .Q(OUT[0]));  // open: Qn, preset, reset, en
  S_R_Flip_Flop s_r_ff_2 (.S(and_3_out), .clk(CLK), .R(and_4_out), .Q(OUT[1]));  // open: Qn, preset, reset, en
endmodule

module _1_bit_reg (
  input  DATA,
  input  LOAD,
  input  CLK,
  output OUT
);

  wire and_1_out, and_2_out, not_1_out;

  not not_1 (not_1_out, DATA);
  and and_1 (and_1_out, DATA, LOAD);
  and and_2 (and_2_out, not_1_out, LOAD);
  S_R_Flip_Flop s_r_ff_1 (.S(and_1_out), .clk(CLK), .R(and_2_out), .Q(OUT));  // open: Qn, preset, reset, en
endmodule

module _16_to_12_bit_conversion (
  input  [15:0] IN,
  output [11:0] OUT
);


  assign OUT = IN[15:4];
endmodule
